# Fritzing sketch strikeball timer (saved by Fritzing 0.9.3b)

parts:
  WeMos_D1_Mini1 = WeMos D1 Mini [part_number=controller]
  R3 = Resistor [tolerance=±5% resistance=15 package="2010 [SMD]"]
  S1 = Round Pushbutton [part_number=team1]
  S2 = Round Pushbutton [part_number=team3]
  S3 = Round Pushbutton [part_number=team2]
  S4 = Toggle Switch [part_number=wifi_enable_switch package=THT]
  LED = RGB LED - (4 legs) [current=20mA package="5 mm [THT]"]
  OLED_I2C1 = OLED 128x64 I2C Monochrome Display [part_number=OLED]
  U1 = Mini-360 DC-DC Buck converter [part_number="DC-DC converter" package=THT]
  R4 = Resistor [tolerance=±5% resistance=15 package="2010 [SMD]"]
  R5 = Resistor [tolerance=±5% resistance=15 package="2010 [SMD]"]
  U2 = Battery Holders [part_number=battery package=lipo-1100mAh]

nets:
  5V: WeMos_D1_Mini1.5V, S4.L2, OLED_I2C1.VDD, U1.OUT+
  N1: WeMos_D1_Mini1.D0, S2.leg1
  N2: WeMos_D1_Mini1.D1, R5.Pin_0
  N3: WeMos_D1_Mini1.D2, R4.Pin_0
  N4: WeMos_D1_Mini1.D3, R3.Pin_0
  N5: WeMos_D1_Mini1.D4, OLED_I2C1.SDA
  N6: WeMos_D1_Mini1.D5, OLED_I2C1.SCK
  N7: WeMos_D1_Mini1.D6, S4.COM
  N8: WeMos_D1_Mini1.D7, S3.leg1
  N9: WeMos_D1_Mini1.D8, S1.leg1
  N10: WeMos_D1_Mini1.G, S1.leg0, S2.leg0, S3.leg0, LED.common_anode, OLED_I2C1.GND, U1.OUT-
  N11: R3.Pin_1, LED.blue_cathode
  N12: LED.red_cathode, R5.Pin_1
  N13: LED.green_cathode, R4.Pin_1
  N14: U1.IN-, U2.-
  N15: U1.IN+, U2.+

custom parts:
  Mini-360 DC-DC Buck converter: Mini-360 DC-DC Buck converter. Tiny buck step down voltage converter, input voltage 4.75 to 23V output 1 to 17V adjustable. Available from ebay and the like.
